// Logisim project Operation Decoder.circ as structural Verilog: 1 circuit, main circuit Operation Decoder
module Operation_Decoder (
  input  [5:0] OP_Code,
  input  [5:0] FUNC_Code
);

  wire add, \and , and_4_out, and_6_out, and_8_out, and_10_out, and_12_out, and_14_out, and_16_out,
       and_17_out, and_18_out, and_19_out, and_20_out, and_21_out, div, divu, mult, mulu, \nor , OP_000000,
       OP_000111, OP_111111, \or , slt, sltu, sub, \xor ;

  // Probe on OP_Code
  // Probe on FUNC_Code
  and and_1 (OP_000000, ~OP_Code[0], ~OP_Code[1], ~OP_Code[2], ~OP_Code[3], ~OP_Code[4], ~OP_Code[5]);  // AND_Gate
  and and_2 (OP_000111, ~OP_Code[0], ~OP_Code[1], ~OP_Code[2], OP_Code[3], OP_Code[4], OP_Code[5]);  // AND_Gate
  and and_3 (OP_111111, OP_Code[0], OP_Code[1], OP_Code[2], OP_Code[3], OP_Code[4], OP_Code[5]);
  and and_4 (and_4_out, ~FUNC_Code[0], ~FUNC_Code[1], ~FUNC_Code[2], ~FUNC_Code[3], ~FUNC_Code[4], FUNC_Code[5]);  // AND_Gate
  and and_5 (add, and_4_out, OP_000000);
  and and_6 (and_6_out, ~FUNC_Code[0], FUNC_Code[1], ~FUNC_Code[2], ~FUNC_Code[3], ~FUNC_Code[4], FUNC_Code[5]);  // AND_Gate
  and and_7 (sub, and_6_out, OP_000000);
  and and_8 (and_8_out, ~FUNC_Code[0], ~FUNC_Code[1], ~FUNC_Code[2], FUNC_Code[3], FUNC_Code[4], ~FUNC_Code[5]);  // AND_Gate
  and and_9 (mult, and_8_out, OP_000000);
  and and_10 (and_10_out, FUNC_Code[0], ~FUNC_Code[1], ~FUNC_Code[2], FUNC_Code[3], FUNC_Code[4], ~FUNC_Code[5]);  // AND_Gate
  and and_11 (mulu, and_10_out, OP_000000);
  and and_12 (and_12_out, ~FUNC_Code[0], FUNC_Code[1], ~FUNC_Code[2], FUNC_Code[3], FUNC_Code[4], ~FUNC_Code[5]);  // AND_Gate
  and and_13 (div, and_12_out, OP_000000);
  and and_14 (and_14_out, FUNC_Code[0], FUNC_Code[1], ~FUNC_Code[2], FUNC_Code[3], FUNC_Code[4], ~FUNC_Code[5]);  // AND_Gate
  and and_15 (divu, and_14_out, OP_000000);
  and and_16 (and_16_out, ~FUNC_Code[0], ~FUNC_Code[1], FUNC_Code[2], ~FUNC_Code[3], ~FUNC_Code[4], FUNC_Code[5]);  // AND_Gate
  and and_17 (and_17_out, FUNC_Code[0], ~FUNC_Code[1], FUNC_Code[2], ~FUNC_Code[3], ~FUNC_Code[4], FUNC_Code[5]);  // AND_Gate
  and and_18 (and_18_out, FUNC_Code[0], FUNC_Code[1], FUNC_Code[2], ~FUNC_Code[3], ~FUNC_Code[4], FUNC_Code[5]);  // AND_Gate
  and and_19 (and_19_out, ~FUNC_Code[0], ~FUNC_Code[1], ~FUNC_Code[2], FUNC_Code[3], ~FUNC_Code[4], FUNC_Code[5]);  // AND_Gate
  and and_20 (and_20_out, ~FUNC_Code[0], FUNC_Code[1], ~FUNC_Code[2], FUNC_Code[3], ~FUNC_Code[4], FUNC_Code[5]);  // AND_Gate
  and and_21 (and_21_out, FUNC_Code[0], FUNC_Code[1], ~FUNC_Code[2], FUNC_Code[3], ~FUNC_Code[4], FUNC_Code[5]);  // AND_Gate
  and and_22 (\and , and_16_out, OP_000000);
  and and_23 (\or , and_17_out, OP_000000);
  and and_24 (\nor , and_18_out, OP_000000);
  and and_25 (\xor , and_19_out, OP_000000);
  and and_26 (slt, and_20_out, OP_000000);
  and and_27 (sltu, and_21_out, OP_000000);

  // Notes on the sheet:
  //   INPUTS
  //   TIpo R
  //   Push/Pop
  //   Specials
  //   ALU 
endmodule
